# Fritzing sketch pest_repeller-v2-schem (saved by Fritzing 0.9.6b)
breadboards: 1

parts:
  ATTINY26L = IC, DIP package, 20 pins [chip_label=IC]
  IC3 = Voltage Regulator [package=to-220-alt]
  R2 = Resistor [tolerance=±5% resistance=470 package="2010 [SMD]"]
  U2 = TRANSISTOR_NPN_2 [package=to-92]
  LED1 = LEDs [package=led10mm]
  R3 = Resistor [tolerance=±5% power=0.5W resistance=100 package=THT]
  LED4 = LEDs [package=led10mm]
  SP1 = SPEAKER [package=pcb_mount_speaker]
  C2 = Ceramic Capacitor [capacitance=100nF voltage=35V package="100 mil [THT, multilayer]"]

nets:
  N1: ATTINY26L.pin4, R2.Pin_1
  5V: ATTINY26L.pin5, ATTINY26L.pin15
  GND: ATTINY26L.pin6, ATTINY26L.pin16, IC3.GND, U2.E, LED1.C, LED4.C, C2.0
  N2: ATTINY26L.pin13, LED1.A
  N3: ATTINY26L.pin14, LED4.A
  12V: IC3.IN, R3.Pin_0, SP1.+
  N4: IC3.OUT, C2.1
  N5: R2.Pin_0, U2.B
  N6: U2.C, R3.Pin_1, SP1.-
